# Fritzing sketch kinoko (saved by Fritzing 0.9.2b)
circuit board: 4.20793cm x 2.73137cm
stripboards: 1

parts:
  LEDS = screw terminal, 3 pins
  Vin = Screw terminal - 2 pins [package=THT]
  CPU = ATTINY45 [package=dip]
  Photoresistor = Screw terminal - 2 pins [package=THT]
  R1 = Resistor [tolerance=±5% resistance=100k package=THT]
  R2 = Resistor [tolerance=±5% resistance=220 package=THT]
  S1 = Momentary Switch [package=ksa_sealed_tac_switch]

nets:
  N1: LEDS.pin1, CPU.PB4(ADC2)
  N2: LEDS.pin2, Vin.pin2, CPU.VCC, R1.Pin_0, S1.3
  N3: LEDS.pin3, Vin.pin1, CPU.GND, Photoresistor.pin1, R2.Pin_1
  N4: CPU.PB5(NRES), Photoresistor.pin2, R1.Pin_1
  N5: CPU.PB3(ADC3), R2.Pin_0, S1.1
